# Fritzing sketch Sketch (saved by Fritzing 0.9.9b)
breadboards: 1

parts:
  MH-ET_LIVE_ESP32_DEVKIT1 = MH-ET LIVE ESP32 DEVKIT 38 pins
  Mod1 = Raspberry Pi 4B
  J1 = Infrared Proximity Sensor

nets:
  GND: MH-ET_LIVE_ESP32_DEVKIT1.GND, Mod1.GND, J1.GND
  N1: MH-ET_LIVE_ESP32_DEVKIT1.TXD0, J1.Vout
  5V: Mod1.5V, J1.Vcc

custom parts:
  MH-ET LIVE ESP32 DEVKIT 38 pins: http://mh.nodebb.com/topic/2/mh-et-live-esp32-devkit
